// Logisim project lcpu.circ as structural Verilog
module main (
);

  wire clock_1_out, CU_p2, CU_p3, CU_p4, CU_p5, CU_p6, CU_p8;
  wire [2:0] undriven_2, undriven_3, undriven_4;
  wire [3:0] CU_p7;
  wire [6:0] CU_p1;
  wire [15:0] imm_q, multiplexer_1_out, multiplexer_2_out, ram_1_data, undriven, undriven_5, undriven_6,
       undriven_7;

  pc_16bit PC (.clock(clock_1_out), .pc(undriven));  // open: addr, op, set, reset, pc_1
  RAM #(.addrWidth(16), .dataWidth(16)) ram_1 (.addr(undriven), .data(ram_1_data));  // open: sel, clk, ld, clr
  id_16bit ID (.inst(ram_1_data), .op(CU_p1), .dreg(undriven_2), .sreg(undriven_3), .treg(undriven_4));
  // control CU: pin names not known; wires that end beside it: CU_p1, CU_p2, CU_p3, CU_p4, CU_p5, CU_p6, CU_p7, CU_p8
  Clock clock_1 (.out(clock_1_out));
  Register #(.width(16)) imm (.D(ram_1_data), .Q(imm_q), .clk(clock_1_out));  // open: en, clr
  registerFile_8x16bit RF (
    .dreg(undriven_2), .sreg(undriven_3), .treg(undriven_4), .dval(undriven_7), .dset(CU_p8),
    .clock(clock_1_out), .sval(undriven_5), .tval(undriven_6));  // open: reg0, reg1, reg2, reg3, reg4, reg5, reg6, reg7
  Multiplexer #(.width(16)) multiplexer_1 (
    .in0(undriven_5), .in1(imm_q), .out(multiplexer_1_out), .sel(CU_p2));  // open: en
  Multiplexer #(.width(16)) multiplexer_2 (
    .in0(undriven_6), .in1({16{1'b0}}), .out(multiplexer_2_out), .sel(CU_p3));  // open: en
  alu_16bit ALU (
    .sval(multiplexer_1_out), .tval(multiplexer_2_out), .cin(CU_p4), .sinv(CU_p5), .tinv(CU_p6), .aop(CU_p7),
    .dval(undriven_7));  // open: gt, eq, lt, cout, zero
endmodule

module registerFile_8x16bit (
  input  [15:0] reg0,
  input  [15:0] reg1,
  input  [15:0] reg2,
  input  [15:0] reg3,
  input  [15:0] reg4,
  input  [15:0] reg5,
  input  [15:0] reg6,
  input  [15:0] reg7,
  input  [2:0] dreg,
  input  clock,
  input  [2:0] sreg,
  input  [2:0] treg,
  input  dset,
  input  [15:0] dval,
  input  [15:0] sval,
  input  [15:0] tval
);

  wire demultiplexer_1_out0, demultiplexer_1_out1, demultiplexer_1_out2, demultiplexer_1_out3,
       demultiplexer_1_out4, demultiplexer_1_out5, demultiplexer_1_out6, demultiplexer_1_out7;

  Demultiplexer #(.select(3)) demultiplexer_1 (
    .out0(demultiplexer_1_out0), .out1(demultiplexer_1_out1), .out2(demultiplexer_1_out2),
    .out3(demultiplexer_1_out3), .out4(demultiplexer_1_out4), .out5(demultiplexer_1_out5),
    .out6(demultiplexer_1_out6), .out7(demultiplexer_1_out7), .in(dset), .sel(dreg));  // open: en
  Register #(.width(16)) register_1 (.D(dval), .en(demultiplexer_1_out0), .Q(reg0), .clk(clock));  // open: clr
  Register #(.width(16)) register_2 (.D(dval), .en(demultiplexer_1_out1), .Q(reg1), .clk(clock));  // open: clr
  Register #(.width(16)) register_3 (.D(dval), .en(demultiplexer_1_out2), .Q(reg2), .clk(clock));  // open: clr
  Register #(.width(16)) register_4 (.D(dval), .en(demultiplexer_1_out3), .Q(reg3), .clk(clock));  // open: clr
  Register #(.width(16)) register_5 (.D(dval), .en(demultiplexer_1_out4), .Q(reg4), .clk(clock));  // open: clr
  Register #(.width(16)) register_6 (.D(dval), .en(demultiplexer_1_out5), .Q(reg5), .clk(clock));  // open: clr
  Register #(.width(16)) register_7 (.D(dval), .en(demultiplexer_1_out6), .Q(reg6), .clk(clock));  // open: clr
  Register #(.width(16)) register_8 (.D(dval), .en(demultiplexer_1_out7), .Q(reg7), .clk(clock));  // open: clr
  Multiplexer #(.select(3), .width(16)) multiplexer_1 (
    .in0(reg0), .in1(reg1), .in2(reg2), .in3(reg3), .in4(reg4), .in5(reg5), .in6(reg6), .in7(reg7),
    .out(sval), .sel(sreg));  // open: en
  Multiplexer #(.select(3), .width(16)) multiplexer_2 (
    .in0(reg0), .in1(reg1), .in2(reg2), .in3(reg3), .in4(reg4), .in5(reg5), .in6(reg6), .in7(reg7),
    .out(tval), .sel(treg));  // open: en
  // Probe on reg0
  // Probe on reg1
  // Probe on reg2
  // Probe on reg3
  // Probe on reg4
  // Probe on reg5
  // Probe on reg6
  // Probe on reg7
endmodule

module alu_16bit (
  input  gt,
  input  eq,
  input  lt,
  input  cin,
  input  cout,
  input  zero,
  input  [15:0] sval,
  input  sinv,
  input  [3:0] aop,
  input  [15:0] tval,
  input  [15:0] dval,
  input  tinv
);

  wire [15:0] adder_1_out, and_1_out, bit_extender_1_out, bit_extender_2_out, bit_extender_3_out, or_1_out,
       shifter_1_out, shifter_2_out, undriven, undriven_2, xor_1_out;

  invertmux_16bit invertmux_16bit_1 (.sval(sval), .invert(sinv), .dval(undriven));
  invertmux_16bit invertmux_16bit_2 (.sval(tval), .invert(tinv), .dval(undriven_2));
  Comparator #(.width(16)) comparator_1 (.a(undriven), .b(undriven_2), .gt(gt), .eq(eq), .lt(lt));
  Adder #(.width(16)) adder_1 (.a(undriven), .b(undriven_2), .out(adder_1_out), .cin(cin), .cout(cout));
  assign and_1_out = undriven & undriven_2;  // AND_Gate and_1, 16 bits wide
  assign or_1_out = undriven | undriven_2;  // OR_Gate or_1, 16 bits wide
  assign xor_1_out = undriven ^ undriven_2;  // XOR_Gate xor_1, 16 bits wide
  assign bit_extender_1_out = {{15{1'b0}}, lt};  // Bit_Extender bit_extender_1
  Shifter #(.width(16)) shifter_1 (.in(undriven), .\dist (undriven_2[3:0]), .out(shifter_1_out));
  Shifter #(.width(16), .shift("lr")) shifter_2 (.in(undriven), .\dist (undriven_2[3:0]), .out(shifter_2_out));
  assign bit_extender_2_out = {{15{1'b0}}, eq};  // Bit_Extender bit_extender_2
  assign bit_extender_3_out = {{15{1'b0}}, gt};  // Bit_Extender bit_extender_3
  Multiplexer #(.select(4), .width(16)) multiplexer_1 (
    .in0(xor_1_out), .in1(or_1_out), .in2(and_1_out), .in3(shifter_2_out), .in4(shifter_1_out),
    .in5(adder_1_out), .in6(bit_extender_1_out), .in7(bit_extender_2_out), .in8(bit_extender_3_out),
    .out(dval), .sel(aop));  // open: in9, in10, in11, in12, in13, in14, in15, en
  or or_2 (zero, dval[0], dval[1], dval[2], dval[3], dval[4], dval[5], dval[6], dval[7], dval[9], dval[10], dval[11], dval[12], dval[13], dval[14], dval[15], dval[8]);
endmodule

module invertmux_16bit (
  input  [15:0] sval,
  input  [15:0] dval,
  input  invert
);

  wire [15:0] not_1_out;

  assign not_1_out = ~sval;  // NOT_Gate not_1, 16 bits wide
  Multiplexer #(.width(16)) multiplexer_1 (.in0(not_1_out), .in1(sval), .out(dval), .sel(invert));  // open: en
endmodule

module pc_16bit (
  input  [15:0] pc,
  input  [1:0] op,
  input  [15:0] pc_1,
  input  [15:0] addr,
  input  set,
  input  clock,
  input  reset
);

  wire [15:0] adder_1_out, adder_2_out, multiplexer_1_out;

  Adder #(.width(16)) adder_1 (.a(pc), .b(16'h1), .out(adder_1_out));  // open: cin, cout
  Adder #(.width(16)) adder_2 (.a(pc), .b(addr), .out(adder_2_out));  // open: cin, cout
  Multiplexer #(.select(2), .width(16)) multiplexer_1 (
    .in0(adder_1_out), .in1(adder_2_out), .in2(addr), .out(multiplexer_1_out), .sel(op));  // open: in3, en
  Register #(.width(16)) register_1 (.D(multiplexer_1_out), .en(set), .Q(pc), .clk(clock), .clr(reset));
  Adder #(.width(16)) adder_3 (.a(pc), .b(16'h1), .out(pc_1));  // open: cin, cout
endmodule

module id_16bit (
  input  [6:0] op,
  input  [2:0] dreg,
  input  [15:0] inst,
  input  [2:0] sreg,
  input  [2:0] treg
);


  assign inst[9:7] = dreg;
  assign op = inst[6:0];
  assign sreg = inst[12:10];
  assign treg = inst[15:13];
endmodule

module control (
  input  ssel,
  input  tsel,
  input  [6:0] cop,
  input  cin,
  input  sinv,
  input  tinv,
  input  [3:0] aop,
  input  dset
);

  wire [7:7] undriven;
  wire [15:0] rom_1_data;

  ROM #(.dataWidth(16)) rom_1 (.addr({undriven[7], cop}), .data(rom_1_data));  // open: sel
  // Pins of 7 and 8 bits meet at {undriven[7], cop}
endmodule
